# Fritzing sketch button_circuit (saved by Fritzing 0.9.3b)
breadboards: 1

parts:
  J1 = Piezo Speaker
  Part1 = Arduino Mega 2560 (Rev3)
  Part2 = Analog Digital MUX Breakout
  R2 = Resistor [tolerance=±5% resistance=1M package=THT]
  J2 = Piezo Speaker
  R3 = Resistor [tolerance=±5% resistance=1M package=THT]

nets:
  GND: J1.pin1, Part1.GND, Part2.GND, R2.Pin_1, J2.pin1, R3.Pin_1
  N1: J1.pin2, R2.Pin_0
  N2: J2.pin2, R3.Pin_0

notes:
  Need to determine resistor - start with 1M
